// Logisim project latch_d_sincronico.circ as structural Verilog: 2 circuits, main circuit LatchD
module LatchD (
  input  D,
  input  E,
  output Qn,
  output Q
);

  wire and_1_out, and_2_out, not_1_out;

  and and_1 (and_1_out, D, E);
  and and_2 (and_2_out, E, not_1_out);
  not not_1 (not_1_out, D);
  nor nor_1 (Qn, and_1_out, Q);
  nor nor_2 (Q, Qn, and_2_out);
endmodule

module FlipFlopD (
  input  D,
  output Q,
  output Qn
);

  wire clk_out, latchd_1_q, not_1_out;

  Clock clk (.out(clk_out));
  not not_1 (not_1_out, clk_out);
  LatchD latchd_1 (.D(D), .E(not_1_out), .Q(latchd_1_q));  // open: Qn
  LatchD latchd_2 (.D(latchd_1_q), .E(clk_out), .Qn(Q), .Q(Qn));
endmodule
