// Logisim project latch_d_sincronico_con_nand.circ as structural Verilog: 1 circuit, main circuit main
module main (
  input  D,
  input  E,
  output Q,
  output Qn
);

  wire nand_1_out, nand_2_out, nand_3_out;

  nand nand_1 (nand_1_out, D, D);
  nand nand_2 (nand_2_out, D, E);
  nand nand_3 (nand_3_out, E, nand_1_out);
  nand nand_4 (Q, nand_2_out, Qn);
  nand nand_5 (Qn, Q, nand_3_out);
endmodule
