// Logisim project latch_d_sincronico_con_nand_con_preset_y_clear_asincronicos.circ as structural Verilog: 1 circuit, main circuit main
module main (
  input  CL,
  input  D,
  input  E,
  input  PR,
  output Q,
  output Qn
);

  wire nand_1_out, nand_2_out, nand_3_out, nand_5_out, nand_6_out;

  nand nand_1 (nand_1_out, D, D);
  nand nand_2 (nand_2_out, D, E);
  nand nand_3 (nand_3_out, E, nand_1_out);
  nand nand_4 (Q, CL, nand_5_out);
  nand nand_5 (nand_5_out, nand_2_out, Qn);
  nand nand_6 (nand_6_out, Q, nand_3_out);
  nand nand_7 (Qn, nand_6_out, PR);
endmodule
