// Logisim project latch_d_sincronico_con_preset_y_clear_asincronico.circ as structural Verilog: 1 circuit, main circuit main
module main (
  input  cl,
  input  D,
  input  E,
  input  pr,
  output Qn,
  output Q
);

  wire and_1_out, and_2_out, nor_1_out, nor_2_out, not_1_out;

  and and_1 (and_1_out, D, E);
  and and_2 (and_2_out, E, not_1_out);
  not not_1 (not_1_out, D);
  nor nor_1 (nor_1_out, and_1_out, Q);
  nor nor_2 (nor_2_out, Qn, and_2_out);
  or or_1 (Qn, cl, nor_1_out);
  or or_2 (Q, nor_2_out, pr);
endmodule
