// Logisim project trabajo_practico_01_ejercicio_01_01_01.circ as structural Verilog: 1 circuit, main circuit main
module main (
  input  x,
  input  y,
  input  z,
  output f
);

  wire not_1_out, not_2_out, not_3_out, or_1_out, or_2_out, or_3_out, or_4_out, or_5_out;

  not not_1 (not_1_out, x);
  not not_2 (not_2_out, y);
  not not_3 (not_3_out, z);
  or or_1 (or_1_out, not_1_out, not_2_out, not_3_out);
  or or_2 (or_2_out, not_1_out, not_2_out, z);
  or or_3 (or_3_out, x, not_2_out, z);
  or or_4 (or_4_out, x, y, not_3_out);
  or or_5 (or_5_out, x, y, z);
  and and_1 (f, or_1_out, or_2_out, or_3_out, or_4_out, or_5_out);
endmodule
