// Logisim project trabajo_practico_01_ejercicio_02_01.circ as structural Verilog: 1 circuit, main circuit main
module main (
  input  [1:0] s,
  input  x,
  output o_1,
  output o_2,
  output o_3,
  output o_4
);

  wire demultiplexer_2_out0, demultiplexer_2_out1;

  Demultiplexer demultiplexer_1 (.out0(o_1), .out1(o_2), .in(demultiplexer_2_out0), .sel(s[0]));
  Demultiplexer demultiplexer_2 (.out0(demultiplexer_2_out0), .out1(demultiplexer_2_out1), .in(x), .sel(s[1]));
  Demultiplexer demultiplexer_3 (.out0(o_3), .out1(o_4), .in(demultiplexer_2_out1), .sel(s[0]));
endmodule
