// Logisim project trabajo_practico_01_ejercicio_02_02.circ as structural Verilog: 1 circuit, main circuit main
module main (
  input  [2:0] s,
  input  x,
  output o_1,
  output o_2,
  output o_3,
  output o_4,
  output o_5,
  output o_6,
  output o_7,
  output o_8
);

  wire demultiplexer_1_out0, demultiplexer_1_out1, demultiplexer_3_out0, demultiplexer_3_out1,
       demultiplexer_6_out0, demultiplexer_6_out1;

  Demultiplexer demultiplexer_1 (.out0(demultiplexer_1_out0), .out1(demultiplexer_1_out1), .in(x), .sel(s[2]));
  Demultiplexer demultiplexer_2 (.out0(o_1), .out1(o_2), .in(demultiplexer_3_out0), .sel(s[0]));
  Demultiplexer demultiplexer_3 (
    .out0(demultiplexer_3_out0), .out1(demultiplexer_3_out1), .in(demultiplexer_1_out0), .sel(s[1]));
  Demultiplexer demultiplexer_4 (.out0(o_3), .out1(o_4), .in(demultiplexer_3_out1), .sel(s[0]));
  Demultiplexer demultiplexer_5 (.out0(o_5), .out1(o_6), .in(demultiplexer_6_out0), .sel(s[0]));
  Demultiplexer demultiplexer_6 (
    .out0(demultiplexer_6_out0), .out1(demultiplexer_6_out1), .in(demultiplexer_1_out1), .sel(s[1]));
  Demultiplexer demultiplexer_7 (.out0(o_7), .out1(o_8), .in(demultiplexer_6_out1), .sel(s[0]));
endmodule
