// Logisim project trabajo_practico_01_ejercicio_02_03.circ as structural Verilog: 1 circuit, main circuit main
module main (
  input  s,
  input  x_0,
  input  x_1,
  input  x_2,
  input  x_3,
  input  x_4,
  input  x_5,
  input  x_6,
  input  x_7,
  output o_1,
  output o_2
);

  Demultiplexer demultiplexer_1 (.out0(o_1), .out1(o_2), .in(x_0), .sel(s));
  Demultiplexer demultiplexer_2 (.out0(o_1), .out1(o_2), .in(x_1), .sel(s));
  Demultiplexer demultiplexer_3 (.out0(o_1), .out1(o_2), .in(x_2), .sel(s));
  Demultiplexer demultiplexer_4 (.out0(o_1), .out1(o_2), .in(x_3), .sel(s));
  Demultiplexer demultiplexer_5 (.out0(o_1), .out1(o_2), .in(x_4), .sel(s));
  Demultiplexer demultiplexer_6 (.out0(o_1), .out1(o_2), .in(x_5), .sel(s));
  Demultiplexer demultiplexer_7 (.out0(o_1), .out1(o_2), .in(x_6), .sel(s));
  Demultiplexer demultiplexer_8 (.out0(o_1), .out1(o_2), .in(x_7), .sel(s));
endmodule
