// Logisim project ejercicio_02_02_f2.circ as structural Verilog: 1 circuit, main circuit main
module main (
  input  x_0,
  input  x_1,
  input  x_2,
  input  x_3,
  input  x_4,
  output f_2
);

  wire and_1_out, and_2_out, and_3_out, not_1_out, not_2_out, not_3_out, not_4_out, not_5_out;

  not not_1 (not_1_out, x_0);
  not not_2 (not_2_out, x_2);
  not not_3 (not_3_out, x_1);
  not not_4 (not_4_out, x_3);
  not not_5 (not_5_out, x_4);
  and and_1 (and_1_out, not_1_out, not_2_out);
  and and_2 (and_2_out, x_1, x_2, not_4_out);
  or or_1 (f_2, and_1_out, and_2_out, and_3_out);
  and and_3 (and_3_out, x_1, not_2_out);
endmodule
