// Logisim project ejercicio_02_03_f1.circ as structural Verilog: 1 circuit, main circuit main
module main (
  input  x_0,
  input  x_1,
  input  x_2,
  input  x_3,
  input  x_4,
  output f_1
);

  wire nand_1_out, nand_2_out, nand_3_out, nand_4_out, nand_5_out, nand_6_out, nand_7_out, nand_8_out,
       nand_9_out, nand_10_out, nand_11_out, nand_12_out, nand_13_out, nand_14_out, nand_15_out, nand_16_out,
       nand_17_out, nand_18_out;

  nand nand_1 (nand_1_out, x_2, x_2);
  nand nand_2 (nand_2_out, x_2, x_2);
  nand nand_3 (nand_3_out, x_0, x_0);
  nand nand_4 (nand_4_out, x_0, x_0);
  nand nand_5 (nand_5_out, x_4, x_4);
  nand nand_6 (nand_6_out, x_4, x_4);
  nand nand_7 (nand_7_out, nand_1_out, x_1);
  nand nand_8 (nand_8_out, nand_7_out, nand_9_out);
  nand nand_9 (nand_9_out, nand_2_out, x_1);
  nand nand_10 (nand_10_out, nand_3_out, x_3, x_4);
  nand nand_11 (nand_11_out, nand_10_out, nand_12_out);
  nand nand_12 (nand_12_out, nand_4_out, x_3, x_4);
  nand nand_13 (nand_13_out, nand_5_out, x_2);
  nand nand_14 (nand_14_out, nand_13_out, nand_15_out);
  nand nand_15 (nand_15_out, nand_6_out, x_2);
  nand nand_16 (nand_16_out, nand_8_out, nand_8_out);
  nand nand_17 (nand_17_out, nand_11_out, nand_11_out);
  nand nand_18 (nand_18_out, nand_14_out, nand_14_out);
  nand nand_19 (f_1, nand_16_out, nand_17_out, nand_18_out);
endmodule
