// Logisim project ejercicio_02_03_f2.circ as structural Verilog: 1 circuit, main circuit main
module main (
  input  x_0,
  input  x_1,
  input  x_2,
  input  x_3,
  input  x_4,
  output f_2
);

  wire nor_1_out, nor_2_out, nor_3_out, nor_4_out, nor_5_out, nor_6_out, nor_8_out;

  nor nor_1 (nor_1_out, x_0, x_2);
  nor nor_2 (nor_2_out, x_1, x_1);
  nor nor_3 (nor_3_out, x_2, x_2);
  nor nor_4 (nor_4_out, x_1, x_1);
  nor nor_5 (nor_5_out, x_2, x_2);
  nor nor_6 (nor_6_out, nor_2_out, x_3, nor_3_out);
  nor nor_7 (f_2, nor_1_out, nor_6_out, nor_8_out);
  nor nor_8 (nor_8_out, nor_4_out, nor_5_out);
endmodule
