// Logisim project ejercicio_02_03_f2.circ as structural Verilog: 1 circuit, main circuit main
module main (
  input  clear,
  input  reset,
  input  set,
  input  preset,
  output Q,
  output Qprima
);

  wire clk_out, nor_1_out, nor_2_out, nor_4_out, nor_5_out, nor_6_out, nor_7_out, nor_8_out, undriven;

  Clock clk (.out(clk_out));
  nor nor_1 (nor_1_out, reset, clk_out);
  nor nor_2 (nor_2_out, clk_out, set);
  // NOR_Gate nor_3 has open pins: in0=nor_1_out, out=open
  nor nor_4 (nor_4_out, nor_2_out, nor_2_out);
  nor nor_5 (nor_5_out, clear, nor_6_out);
  nor nor_6 (nor_6_out, undriven, Qprima);
  nor nor_7 (nor_7_out, Q, nor_4_out);
  nor nor_8 (nor_8_out, nor_7_out, preset);
  nor nor_9 (Q, nor_5_out, nor_5_out);
  nor nor_10 (Qprima, nor_8_out, nor_8_out);
endmodule
